// Logisim project base.circ as structural Verilog: 2 circuits, main circuit main
module main (
  input  in_1,
  input  in_2,
  input  in_3,
  input  in_4
);

  wire n4511_1_a_2, n4511_1_b_2, n4511_1_c_2, n4511_1_d_2, n4511_1_e, n4511_1_f, n4511_1_g;

  _4511 u_4511_1 (
    .D(in_1), .C(in_2), .B(in_3), .A(in_4), .a_2(n4511_1_a_2), .b_2(n4511_1_b_2), .c_2(n4511_1_c_2),
    .d_2(n4511_1_d_2), .e(n4511_1_e), .f(n4511_1_f), .g(n4511_1_g));
  _7_Segment_Display u_7_segment_display_1 (
    .g(n4511_1_g), .f(n4511_1_f), .a(n4511_1_a_2), .b(n4511_1_b_2), .d(n4511_1_d_2), .c(n4511_1_c_2));  // open: e, dp
endmodule

module _4511 (
  input  D,
  input  C,
  input  B,
  input  A,
  output a_2,
  output b_2,
  output c_2,
  output d_2,
  output e,
  output f,
  output g
);

  wire nand_1_out, nand_5_out, nand_6_out, nand_7_out, nand_10_out, nand_11_out;

  nand nand_1 (nand_1_out, D, D);
  nand nand_2 (b_2, D, D);
  nand nand_3 (c_2, B, B);
  nand nand_4 (d_2, A, A);
  nand nand_5 (nand_5_out, D, D);
  nand nand_6 (nand_6_out, B, B);
  nand nand_7 (nand_7_out, A, A);
  nand nand_8 (a_2, A, nand_1_out);
  nand nand_9 (e, A, nand_5_out);
  nand nand_10 (nand_10_out, nand_6_out, nand_7_out);
  nand nand_11 (nand_11_out, D, D);
  nand nand_12 (f, nand_10_out, nand_11_out);

  assign g = B;
endmodule
