// Logisim project example-2-flip-flop-counter.circ as structural Verilog: 1 circuit, main circuit main
module main (
  input  in_1
);

  wire clock_1_out, j_k_ff_1_q, j_k_ff_2_q, j_k_ff_2_qn, j_k_ff_3_q, j_k_ff_3_qn, j_k_ff_4_q, j_k_ff_4_qn,
       n7_segment_display_driver_1_a_2, n7_segment_display_driver_1_b_2, n7_segment_display_driver_1_c_2,
       n7_segment_display_driver_1_d_2, n7_segment_display_driver_1_e, n7_segment_display_driver_1_f,
       n7_segment_display_driver_1_g;

  Clock clock_1 (.out(clock_1_out));
  J_K_Flip_Flop j_k_ff_1 (.J(in_1), .clk(j_k_ff_2_qn), .K(in_1), .Q(j_k_ff_1_q));  // open: Qn, preset, en, reset
  J_K_Flip_Flop j_k_ff_2 (
    .J(in_1), .clk(j_k_ff_3_qn), .K(in_1), .Q(j_k_ff_2_q), .Qn(j_k_ff_2_qn));  // open: preset, en, reset
  J_K_Flip_Flop j_k_ff_3 (
    .J(in_1), .clk(j_k_ff_4_qn), .K(in_1), .Q(j_k_ff_3_q), .Qn(j_k_ff_3_qn));  // open: preset, en, reset
  J_K_Flip_Flop j_k_ff_4 (
    .J(in_1), .clk(clock_1_out), .K(in_1), .Q(j_k_ff_4_q), .Qn(j_k_ff_4_qn));  // open: preset, en, reset
  _7_segment_display_driver u_7_segment_display_driver_1 (
    .D(j_k_ff_1_q), .C(j_k_ff_2_q), .B(j_k_ff_3_q), .A(j_k_ff_4_q), .a_2(n7_segment_display_driver_1_a_2),
    .b_2(n7_segment_display_driver_1_b_2), .c_2(n7_segment_display_driver_1_c_2),
    .d_2(n7_segment_display_driver_1_d_2), .e(n7_segment_display_driver_1_e),
    .f(n7_segment_display_driver_1_f), .g(n7_segment_display_driver_1_g));
  _7_Segment_Display u_7_segment_display_1 (
    .g(n7_segment_display_driver_1_g), .f(n7_segment_display_driver_1_f),
    .a(n7_segment_display_driver_1_a_2), .b(n7_segment_display_driver_1_b_2),
    .e(n7_segment_display_driver_1_e), .d(n7_segment_display_driver_1_d_2),
    .c(n7_segment_display_driver_1_c_2));  // open: dp

  // Notes on the sheet:
  //   Visit: http://github.com/marceloboeira for more examples
endmodule
